// Logisim project 1011 Sequence Detector.circ as structural Verilog: 1 circuit, main circuit main
module main (
  input  Input
);

  wire and_1_out, and_2_out, and_3_out, clock_1_out, D0_q, D0_qn, D1_q, not_1_out, or_1_out;

  not not_1 (not_1_out, Input);
  Clock clock_1 (.out(clock_1_out));
  and and_1 (and_1_out, not_1_out, D0_q);
  or or_1 (or_1_out, and_1_out, and_2_out);
  and and_2 (and_2_out, Input, D0_qn, D1_q);
  D_Flip_Flop D1 (.clk(clock_1_out), .D(or_1_out), .Q(D1_q));  // open: Qn, preset, en, reset
  // Probe on D1_q
  // Probe on D0_q
  D_Flip_Flop D0 (.clk(clock_1_out), .D(Input), .Q(D0_q), .Qn(D0_qn));  // open: preset, en, reset
  and and_3 (and_3_out, Input, D0_q, D1_q);
  LED led_1 (.in(and_3_out));

  // Notes on the sheet:
  //   Clock
  //   Ankit Kumar
  //   Probe
  //   1011 Sequence Detector
  //   Output
endmodule
