// Logisim project Mealy_fsm.circ as structural Verilog: 1 circuit, main circuit main
module main (
  input  INPUT,
  input  RESET
);

  wire and_1_out, clock_1_out, d_ff_1_q, xor_1_out;

  xor xor_1 (xor_1_out, d_ff_1_q, INPUT);
  Clock clock_1 (.out(clock_1_out));
  D_Flip_Flop d_ff_1 (.clk(clock_1_out), .D(xor_1_out), .Q(d_ff_1_q), .en(RESET));  // open: Qn, preset, reset
  and and_1 (and_1_out, INPUT, d_ff_1_q);
  LED led_1 (.in(and_1_out));

  // Notes on the sheet:
  //   CLOCK
  //   Output High only when input = 1 and current state is S1
  //   Ankit Kumar
  //   OUTPUT
endmodule
