// Logisim project Traffic Light.circ as structural Verilog: 1 circuit, main circuit main
module main (
  input  INPUT,
  input  RESET
);

  wire and_1_out, and_2_out, and_3_out, and_4_out, and_5_out, and_6_out, and_7_out, clock_1_out, D0_q, D0_qn,
       D1_q, D1_qn, not_1_out, or_1_out, or_2_out;

  Clock clock_1 (.out(clock_1_out));
  and and_1 (and_1_out, D0_qn, not_1_out, D1_q);
  not not_1 (not_1_out, INPUT);
  and and_2 (and_2_out, INPUT, D1_qn, D0_q);
  or or_1 (or_1_out, and_1_out, and_2_out);
  and and_3 (and_3_out, D0_qn, INPUT, D1_qn);
  and and_4 (and_4_out, not_1_out, D0_q, D1_q);
  D_Flip_Flop D1 (.clk(clock_1_out), .D(or_1_out), .Q(D1_q), .Qn(D1_qn), .en(RESET));  // open: preset, reset
  or or_2 (or_2_out, and_3_out, and_4_out);
  D_Flip_Flop D0 (.clk(clock_1_out), .D(or_2_out), .Q(D0_q), .Qn(D0_qn), .reset(RESET));  // open: preset, en
  LED led_1 (.in(and_5_out));
  and and_5 (and_5_out, D0_qn, D1_qn);
  and and_6 (and_6_out, D0_q, D1_qn);
  LED led_2 (.in(and_6_out));
  LED led_3 (.in(and_7_out));
  and and_7 (and_7_out, D0_qn, D1_q);

  // Notes on the sheet:
  //   CLOCK
  //   Ankit Kumar
  //   TRAFFIC LIGHT CONTROLLER
  //   RED
  //   Green
  //   Yellow
endmodule
