// Logisim project fsm_4state.circ as structural Verilog: 1 circuit, main circuit main
module main (
  input  in_1
);

  wire clock_1_out, d_ff_1_q, d_ff_2_q, d_ff_2_qn, xor_1_out;

  xor xor_1 (xor_1_out, d_ff_1_q, d_ff_2_q);
  Clock clock_1 (.out(clock_1_out));
  D_Flip_Flop d_ff_1 (.clk(clock_1_out), .D(xor_1_out), .Q(d_ff_1_q), .en(in_1));  // open: Qn, preset, reset
  D_Flip_Flop d_ff_2 (
    .clk(clock_1_out), .D(d_ff_2_qn), .Q(d_ff_2_q), .Qn(d_ff_2_qn), .en(in_1));  // open: preset, reset

  // Notes on the sheet:
  //   D1
  //   Cycles Through 4 States After Every Clock
  //   RESET
  //   Ankit Kumar
  //   D2
endmodule
